# Fritzing sketch schema_frizting_DegrooteMedric (saved by Fritzing 0.9.4)
breadboards: 1

parts:
  Onderdeel1 = Adafruit T-Cobbler Plus [part_number="Adafruit #1989 and #2028"]
  U1 = PCF8574 [package="DIP16 [THT]"]
  LCD1 = LCD screen
  U2 = POT [package=pot_mammoth]
  Onderdeel2 = InvenSense MPU6050
  S1 = SWITCH-MOMENTARY-2 [package=tactile-pth-12mm]
  R1 = Resistor [tolerance=±5% resistance=220 package="0603 [SMD]"]
  SM1 = 28BYJ-48 Stepper Motor [part_number=28BYJ-48]
  Driver1 = 28BYJ-48 Driver Module [part_number=ULN2003 package=THT]
  Laser_Transmitter_Module1 = Laser Transmitter Module [part_number="Laser Transmitter Module" chip_label=IC package="DIP (Dual Inline) [THT]"]
  Laser_Sensor_Module3 = Laser Sensor Module [part_number="Laser Sensor Module" chip_label=IC package="DIP (Dual Inline) [THT]"]
  R5 = Resistor [tolerance=±5% resistance=10k package="0603 [SMD]"]
  R6 = Photocell (LDR) [package=THT]
  ADC2 = MCP3008 [package=dil16]
  RE1 = KY-040 Rotary encoder [package=THT]
  R7 = Resistor [tolerance=±5% resistance=220 package=THT]
  YwRobot_Power_Supply1 = YwRobot Breadboard Power Supply [part_number=545043]
  Onderdeel9 = Arduino Uno (Rev3)
  Onderdeel10 = Logic Level Converter
  Mod2 = KY-035 Analog Magnetic Hall Sensor [package="Breakout board"]
  Onderdeel11 = GY-VL53L0XV2 Laser Ranger Module
  R8 = PHOTOCELL [package=photocell]
  R9 = PHOTOCELL [package=photocell]

nets:
  N1: Onderdeel1.SDA, U1.SDA, Onderdeel2.SDA
  N2: Onderdeel1.SCL, U1.SCL, Onderdeel2.SCL
  N3: Onderdeel1.GPIO4, Driver1.IN1
  GND: Onderdeel1.GND, LCD1.VSS, LCD1.R/W, LCD1.LED-, U2.S, Onderdeel2.GND, R1.Pin_0, Driver1.GND, R6.pin_1, ADC2.DGND, ADC2.AGND, RE1.GND, YwRobot_Power_Supply1.GND, Onderdeel10.GND, Mod2.-, R8.P$2
  N4: Onderdeel1.GPIO17, Driver1.IN2
  N5: Onderdeel1.GPIO27, Driver1.IN3
  N6: Onderdeel1.GPIO22, Driver1.IN4
  N7: Onderdeel1.MOSI, ADC2.Din
  N8: Onderdeel1.MISO, ADC2.Dout
  N9: Onderdeel1.SCLK, ADC2.CLK
  N10: Onderdeel1.GPIO6, S1.1
  N11: Onderdeel1.GPIO13, R7.Pin_1
  N12: Onderdeel1.GPIO19, RE1.DT
  N13: Onderdeel1.GPIO26, RE1.CLK
  N14: Onderdeel1.TXD, Onderdeel10.TX_HV
  N15: Onderdeel1.RXD, Onderdeel10.RX_LV
  N16: Onderdeel1.GPIO23, LCD1.RS
  N17: Onderdeel1.GPIO24, LCD1.E
  N18: Onderdeel1.CE0, ADC2.CS/SHDN
  N19: Onderdeel1.GPIO21, R9.P$2
  N20: U1.A0, U1.A1, U1.A2, U1.GND
  N21: U1.P0, LCD1.DB0
  N22: U1.P1, LCD1.DB1
  N23: U1.P2, LCD1.DB2
  N24: U1.P3, LCD1.DB3
  N25: U1.P4, LCD1.DB4
  N26: U1.P5, LCD1.DB5
  N27: U1.P6, LCD1.DB6
  N28: U1.P7, LCD1.DB7
  N29: LCD1.VDD, LCD1.LED+, U2.E, Driver1.Vmotor, YwRobot_Power_Supply1.VCC#10
  N30: LCD1.V0, U2.A
  VCC: Onderdeel2.VCC, R5.Pin_1, ADC2.VREF, ADC2.VDD, RE1.Vcc, YwRobot_Power_Supply1.VCC#6, Onderdeel10.LV, Mod2.Vin
  N31: S1.2, R1.Pin_1
  N32: SM1.blue-pin, Driver1.blue-pin
  N33: SM1.pink-pin, Driver1.pink-pin
  N34: SM1.yellow-pin, Driver1.yellow-pin
  N35: SM1.orange-pin, Driver1.orange-pin
  N36: SM1.red-pin, Driver1.red-pin
  VCC_2: Laser_Transmitter_Module1.VCC, Laser_Sensor_Module3.VCC, Onderdeel9.5V
  GND_2: Laser_Transmitter_Module1.GND, Laser_Sensor_Module3.GND, Onderdeel9.GND
  N37: Laser_Sensor_Module3.OUT, R9.P$1
  N38: R5.Pin_0, R6.pin_0, ADC2.CH0
  N39: ADC2.CH1, Mod2.S
  N40: RE1.SW, R7.Pin_0
  N41: Onderdeel9.A4/SDA, Onderdeel9.A5/SCL, Onderdeel11.GPIO1
  N42: Onderdeel9.D0/RX, Onderdeel10.TX_LV
  N43: Onderdeel9.D1/TX, Onderdeel10.RX_HV

notes:
  blauw = gpio datalijne
  bruin = SDA
  geel = SCL
  roze = MCP data
  rood = 5V
  zwart = gnd
  oranje = 3.3V
  groen = LCD 5-8
  paars =LCD 1-4
  MCP3008 voor lichtweerstand in te lezen met weerstand ervoor en magneetsensor
  stappenmotor op 5V (zonder transistor?)
  lasersstralen via transistor (voorlopig op 3.3V maar kan zijn dak op 5V ga moeten overspringen
  de lasersensoren zitten niet in een aparte kring, ik kan ze ook eventueel in de transistorkring steken maar zal wel lukken op deze manier
  L to R ->
  MPU6050 button off
  pot LCD
  Rotary
  externe voeding, deze staat er, maar op voeding raspi is zelfde
  weerstandsdeling
  5k en 10kohm
  SDA, SCL for TOF sensor

custom parts:
  Adafruit T-Cobbler Plus: The Raspberry Pi has landed on the Maker World like a 40-GPIO pinned, quad-USB ported, credit card sized bomb of DIY joy. And while you can use most of our great Model B accessories by hooking up our downgrade cable, its probably a good time to upgrade your set up and accessorize using all of the 40 pins. That's why we now carry the Assembled Adafruit Pi T-Cobbler Plus - Breakout + Cable for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
  28BYJ-48 Stepper Motor: Unipolar Stepper Motor 28BYJ-48 Top coil - pink & orange Bottom coil - blue & yellow Common rail - red Connector pins: blue - pink - yellow - orange - red
  28BYJ-48 Driver Module: ULN2003 Driver Module for the 28BYJ-48 Unipolar Stepper Motor LED A - Blue wire - Bottom coil left LED B - Pink wire - Top coil left LED C - Yellow wire - Bottom coil right LED D - Orange wire - Top coil right Common rail - red Connector pins: blue - pink - yellow - orange - red Control pins - IN1 to IN4 Power pins - GND & Vmotor (5-12V) On/Off jumper (if removed, power to motor is cut).
  Laser Transmitter Module: Red Laser Transmitter Module Power Input: 5V DC Laser: KY-008 Wavelenght: 650nm
  Laser Sensor Module: Laser Sensor/Detector/Receiver Module Working Voltage: 5V
  KY-040 Rotary encoder: KY-040 Rotary Encoder with switch on breakout borad from AZ Delivery
  YwRobot Breadboard Power Supply: The YwRobot Breadboard Power Supply (MB-V2) has two power rails; they can be 5V or 3V3. Power to the module can be provided through the female USB socket or through the A10 (female) 2.1mm power jack.
  KY-035 Analog Magnetic Hall Sensor: KY-035 analog magnetic hall sensor is a module that reacts in the presence of a magnet. It can measure the polarity and relative strength of a magnetic field.
  GY-VL53L0XV2 Laser Ranger Module: The GY-VL53L0XV2 is based on the VL53L0X from ST Microelectronics, a time-of-flight ranging system integrated into a compact module.
